# Fritzing sketch Circuito_TwoWayCom_ESP_NOW (saved by Fritzing 0.9.3b)
breadboards: 2

parts:
  U1 = ESP32-38PinWide [part_number=ESP32-38PinWide]
  ZS-042_RTC1 = ZS-042 RTC Module
  Squix1 = OLED 0.96" 128x64 I2C SSD1306
  U2 = LuaNode32 / ESP32
  BMP280_Breakout1 = BMP280 Breakout Board [part_number=BMP280]
  Squix2 = OLED 0.96" 128x64 I2C SSD1306

nets:
  VCC: U1.3.3, ZS-042_RTC1.VCC, Squix1.VCC
  GND: U1.GND, ZS-042_RTC1.GND, Squix1.GND
  N1: U1.GPIO21, ZS-042_RTC1.SDA, Squix1.SCA
  N2: U1.GPIO22, ZS-042_RTC1.SCL, Squix1.SCL
  GND_2: U2.GND, BMP280_Breakout1.GND, Squix2.GND
  VCC_2: U2.3V3, BMP280_Breakout1.VCC, Squix2.VCC
  N3: U2.D21, BMP280_Breakout1.SDA, Squix2.SCA
  N4: U2.D22, BMP280_Breakout1.SCL, Squix2.SCL

notes:
  Module 1:
  ESP32 (38 pins), DS3231 and 128x64 OLED display.
  Receives the data from the module 2.
  Sends the strings of date, time and temperature to the module 2.
  ESP32 (30 pins), BMP280 and 128x64 OLED display.
  Receives the data from module 1.
  Sends the data of temperature and air pressure to module 1.

custom parts:
  ESP32-38PinWide: Generic 38-Pin ESP32 with wide format (only access to one side of pins on a breadboard) based on Stephen Lilley's HiLetgo ESP-WROOM-32 ESP32 ESP-32S Development Board.
  LuaNode32 / ESP32: ESP32 based LuaNode32
  BMP280 Breakout Board: This is a breakout board for the Bosch Sensortec BMP280, "an absolute barometric pressure sensor especially designed for mobile applications." The operation range is 300 to 1100 hPa. Supply voltage is 1.2 to 3.6V. Operating temperature range is -40 to +85 °C.
